// Logisim project TAREA1_DIGITALES.circ as structural Verilog: 1 circuit, main circuit main
module main (
  input  A,
  input  B,
  input  C,
  output S,
  output Cout
);

  wire and_1_out, and_2_out, xor_1_out;

  xor xor_1 (xor_1_out, A, B);
  xor xor_2 (S, xor_1_out, C);
  and and_1 (and_1_out, xor_1_out, C);
  and and_2 (and_2_out, B, A);
  or or_1 (Cout, and_1_out, and_2_out);

  // Notes on the sheet:
  //   A'B+B'A
  //   S=[(A'B+B'A)' * C]+[C' * (A'B+B'A)]
  //   (A'B+B'A) * C
  //   A * B
  //   [(A'B+B'A)*C] + (A*B)
endmodule
